// Logisim project micro.circ as structural Verilog: 1 circuit, main circuit EV20_Superescalar
module EV20_Superescalar (
  input  in_1
);

  wire and_1_out, bloque1_1_preload, CLK, CLK2, CLK3, CLK4, dipswitch_1_sw1, not_1_out, not_2_out, or_1_out,
       pipeline_register_1_p16, pipeline_register_1_p19, pipeline_register_2_p17, pipeline_register_3_p7,
       register_1_q, selector_d_1_p2, uc1_1_aluenable, uc1_1_loadstoreenable, undriven, undriven_2,
       undriven_3, undriven_5, undriven_6;
  wire [1:0] LoadStore_p13, LoadStore_p15, pipeline_register_1_p12, pipeline_register_1_p14,
       pipeline_register_2_p13, pipeline_register_2_p15, undriven_4;
  wire [3:0] LoadStore_p12, pipeline_register_1_p11, pipeline_register_2_p12;
  wire [5:0] LoadStore_p16, LoadStore_p18, LoadStore_p19, LoadStore_p20, multiplexer_3_out,
       multiplexer_4_out, multiplexer_5_out, pipeline_register_1_p15, pipeline_register_1_p17,
       pipeline_register_1_p18, pipeline_register_2_p16, pipeline_register_2_p18, pipeline_register_2_p19,
       pipeline_register_2_p20, reg_C_address, selector_a_1_busasel, selector_b_1_out_2,
       selector_c_1_busc_selector;
  wire [8:8] LoadStore_p14, pipeline_register_1_p13, pipeline_register_2_p14;
  wire [9:0] LoadStore_p17, register_2_q;
  wire [10:0] ProgramCounterReg_pc;
  wire [14:0] MicroInstructionROM_microinstruction, multiplexer_2_out;
  wire [15:0] ALUALULAU_z, BusA_ALU_q, BusA_LS_q, BusB_ALU_q, Constant_K_q, data_1_datamemout,
       multiplexer_1_out, reg_A_read, reg_B_read, reg_C_write, selector_k_1_constante_k;
  wire [23:0] BBUS, ProgramMemory_data;

  // Probe on ProgramCounterReg_pc
  DipSwitch #(.number(2)) dipswitch_1 (.sw1(dipswitch_1_sw1));  // open: sw2
  ROM #(.addrWidth(11), .dataWidth(24)) ProgramMemory (.addr(ProgramCounterReg_pc), .data(ProgramMemory_data));
  // Probe on undriven
  // Probe on undriven_2
  // Probe on undriven_3
  // Probe on undriven_4[1]
  // Probe on undriven_4[0]
  // Probe on undriven_5
  Bloque1 bloque1_1 (.jump_type(BBUS[21:20]), .register_to_test(16'hfff), .Preload(bloque1_1_preload));  // open: CY
  ClockGenerator clocks (.Auto(dipswitch_1_sw1), .ManualCLK(in_1), .CLK(CLK), .CLK2(CLK2), .CLK3(CLK3), .CLK4(CLK4));
  and and_1 (and_1_out, BBUS[22], bloque1_1_preload);
  Register #(.width(24)) InstructionRegister (.D(ProgramMemory_data), .en(1'b1), .clk(CLK), .Q(BBUS));  // open: clr
  PCreg ProgramCounterReg (
    .PC(ProgramCounterReg_pc), .HOLD(1'b0), .Preload(and_1_out), .CLK1(CLK),
    .displacement_or_address(BBUS[15:5]));
  // Probe on BBUS
  // Probe on reg_A_read
  // Probe on reg_B_read
  Selector_B selector_b_1 (.in_1(BBUS), .out_2(selector_b_1_out_2));
  Micro_Instruction_ROM MicroInstructionROM (
    .Instruction(BBUS), .MicroInstruction(MicroInstructionROM_microinstruction));
  // Selector_D selector_d_1: pin names not known; wires that end beside it: BBUS, selector_d_1_p2
  Selector_A selector_a_1 (.BusB(BBUS), .BusASel(selector_a_1_busasel));
  Selector_C selector_c_1 (.BusB(BBUS), .BusC_Selector(selector_c_1_busc_selector));
  selector_K selector_k_1 (.instruction_register(BBUS), .constante_K(selector_k_1_constante_k));
  register_bank register_bank_1 (
    .register_out_B_data(reg_B_read), .register_out_A_address(pipeline_register_1_p17),
    .register_out_B_address(pipeline_register_1_p18), .register_out_A_data(reg_A_read),
    .register_in_data(reg_C_write), .register_in_address(reg_C_address));  // open: clk, register_out_aux_address, register_out_aux_data
  // Probe on MicroInstructionROM_microinstruction[14:11]
  // Probe on MicroInstructionROM_microinstruction[10:9]
  // Probe on MicroInstructionROM_microinstruction[8]
  // Probe on MicroInstructionROM_microinstruction[7]
  // Probe on MicroInstructionROM_microinstruction[6]
  // Probe on MicroInstructionROM_microinstruction[5:0]
  Register #(.width(16), .trigger("falling")) Constant_K (
    .D(selector_k_1_constante_k), .clk(CLK2), .Q(Constant_K_q));  // open: en, clr
  // Pipeline_register pipeline_register_1: pin names not known; wires that end beside it: MicroInstructionROM_microinstruction[14:11], MicroInstructionROM_microinstruction[10:9], MicroInstructionROM_microinstruction[8], MicroInstructionROM_microinstruction[7:6], MicroInstructionROM_microinstruction[5:0], selector_d_1_p2, selector_a_1_busasel, selector_b_1_out_2, selector_c_1_busc_selector, CLK2, pipeline_register_1_p11, pipeline_register_1_p12, pipeline_register_1_p13[8], pipeline_register_1_p14, pipeline_register_1_p15, pipeline_register_1_p16, pipeline_register_1_p17, pipeline_register_1_p18, pipeline_register_1_p19
  or or_1 (or_1_out, MicroInstructionROM_microinstruction[7], MicroInstructionROM_microinstruction[6]);
  Multiplexer #(.width(16), .enable("false")) multiplexer_1 (
    .in0(reg_A_read), .in1(Constant_K_q), .out(multiplexer_1_out), .sel(or_1_out));
  Register #(.width(16)) BusA_ALU (
    .D(multiplexer_1_out), .en(uc1_1_aluenable), .clk(CLK2), .Q(BusA_ALU_q));  // open: clr
  // Probe on pipeline_register_1_p11
  // Probe on pipeline_register_1_p12
  // Probe on pipeline_register_1_p13[8]
  // Probe on pipeline_register_1_p14[1]
  // Probe on pipeline_register_1_p14[0]
  // Probe on pipeline_register_1_p15
  Register #(.width(16)) BusB_ALU (.D(reg_B_read), .en(uc1_1_aluenable), .clk(CLK2), .Q(BusB_ALU_q));  // open: clr
  // Probe on BusA_ALU_q
  // Probe on BusB_ALU_q
  UC1 uc1_1 (
    .MRyMW_OUT_E1(pipeline_register_1_p14), .ALUEnable(uc1_1_aluenable),
    .LoadStoreEnable(uc1_1_loadstoreenable));  // open: HOLD, ALUisFree, MEMisFree
  ALU ALUALULAU (.ALUC(pipeline_register_2_p12), .A(BusA_ALU_q), .B(BusB_ALU_q), .Z(ALUALULAU_z));  // open: CYin, CYout
  // Probe on ALUALULAU_z
  Register #(.width(1)) register_1 (.D(uc1_1_loadstoreenable), .clk(CLK2), .Q(register_1_q));  // open: en, clr
  not not_1 (not_1_out, uc1_1_aluenable);
  not not_2 (not_2_out, uc1_1_loadstoreenable);
  Register #(.width(10)) register_2 (
    .D(LoadStore_p17), .en(uc1_1_loadstoreenable), .clk(CLK2), .Q(register_2_q));  // open: clr
  Register #(.width(16)) BusA_LS (.D(reg_A_read), .en(uc1_1_loadstoreenable), .clk(CLK2), .Q(BusA_LS_q));  // open: clr
  // Pipeline_register pipeline_register_2: pin names not known; wires that end beside it: pipeline_register_1_p11, pipeline_register_1_p12, pipeline_register_1_p13[8], pipeline_register_1_p14, pipeline_register_1_p15, pipeline_register_1_p16, pipeline_register_1_p17, pipeline_register_1_p18, pipeline_register_1_p19, not_1_out, CLK3, pipeline_register_2_p12, pipeline_register_2_p13, pipeline_register_2_p14[8], pipeline_register_2_p15, pipeline_register_2_p16, pipeline_register_2_p17, pipeline_register_2_p18, pipeline_register_2_p19, pipeline_register_2_p20
  // Pipeline_register LoadStore: pin names not known; wires that end beside it: pipeline_register_1_p11, pipeline_register_1_p12, pipeline_register_1_p13[8], pipeline_register_1_p14, pipeline_register_1_p15, pipeline_register_1_p16, pipeline_register_1_p17, pipeline_register_1_p18, pipeline_register_1_p19, not_2_out, CLK3, LoadStore_p12, LoadStore_p13, LoadStore_p14[8], LoadStore_p15, LoadStore_p16, LoadStore_p17, LoadStore_p18, LoadStore_p19, LoadStore_p20
  Data data_1 (
    .DAddress(register_2_q), .clk(CLK2), .Enable(register_1_q), .DataMemInput(BusA_LS_q),
    .DataMemOut(data_1_datamemout));  // open: M
  // Probe on pipeline_register_2_p12
  // Probe on pipeline_register_2_p13
  // Probe on pipeline_register_2_p14[8]
  // Probe on pipeline_register_2_p15[1]
  // Probe on pipeline_register_2_p15[0]
  // Probe on pipeline_register_2_p16
  // Probe on LoadStore_p12
  // Probe on LoadStore_p13
  // Probe on LoadStore_p14[8]
  // Probe on LoadStore_p15[1]
  // Probe on LoadStore_p15[0]
  // Probe on LoadStore_p16
  Multiplexer #(.width(15), .enable("false")) multiplexer_2 (
    .in0({pipeline_register_2_p12, pipeline_register_2_p13, pipeline_register_2_p14[8], pipeline_register_2_p15, pipeline_register_2_p16}),
    .in1({LoadStore_p12, LoadStore_p13, LoadStore_p14[8], LoadStore_p15, LoadStore_p16}),
    .out(multiplexer_2_out), .sel(undriven_6));
  Multiplexer #(.width(6), .enable("false")) multiplexer_3 (
    .in0(pipeline_register_2_p18), .in1(LoadStore_p18), .out(multiplexer_3_out), .sel(undriven_6));
  Multiplexer #(.width(6), .enable("false")) multiplexer_4 (
    .in0(pipeline_register_2_p19), .in1(LoadStore_p19), .out(multiplexer_4_out), .sel(undriven_6));
  Multiplexer #(.width(6), .enable("false")) multiplexer_5 (
    .in0(pipeline_register_2_p20), .in1(LoadStore_p20), .out(multiplexer_5_out), .sel(undriven_6));
  // Pipeline_register pipeline_register_3: pin names not known; wires that end beside it: multiplexer_2_out[14:11], multiplexer_2_out[10:9], multiplexer_2_out[8], multiplexer_2_out[7:6], multiplexer_2_out[5:0], multiplexer_5_out, pipeline_register_3_p7, multiplexer_3_out, multiplexer_4_out

  // Other names for the same wires on the sheet: pulseGenManual = in_1

  // Notes on the sheet:
  //   contents of ProgramMemory (hex, n*v repeats v):
  //   80464 80443 80464 80443
  //   splitters que encajar con los registros de pipeline
  //   para hacer copy-paste
  //   probes que encajar en los splitters de arriba
  //   INSTRUCTION
  //   REGISTER
  //   //todo: condensar los selectores en un solo bloque
  //   uc3
endmodule
